// Logisim project ep3a.circ as structural Verilog: 1 circuit, main circuit main
module main (
  input  [15:0] _1,
  input  _9,
  input  inc_1,
  input  reset_1,
  input  write_0_read_1,
  input  _0__destino_0___1__destino_1
);

  wire clock_1_out, not_1_out;
  wire [7:0] counter_1_q;
  wire [15:0] bit_extender_1_out, demultiplexer_1_out0, demultiplexer_1_out1, multiplexer_1_out,
       multiplexer_2_out, ram_1_data;

  Clock clock_1 (.out(clock_1_out));
  Multiplexer #(.width(16)) multiplexer_1 (
    .in0(bit_extender_1_out), .in1(_1), .out(multiplexer_1_out), .sel(_9));  // open: en
  Counter counter_1 (.count(inc_1), .Q(counter_1_q), .clk(clock_1_out), .clr(reset_1));  // open: load, D, carry
  assign bit_extender_1_out = {{8{1'b0}}, counter_1_q};  // Bit_Extender bit_extender_1
  RAM #(.dataWidth(16), .bus("separate")) ram_1 (
    .addr(counter_1_q), .din(multiplexer_1_out), .data(ram_1_data), .clk(clock_1_out), .ld(write_0_read_1));  // open: str, sel, clr
  Multiplexer #(.width(16)) multiplexer_2 (
    .in0(ram_1_data), .in1(multiplexer_1_out), .out(multiplexer_2_out), .sel(not_1_out));  // open: en
  not not_1 (not_1_out, write_0_read_1);
  Demultiplexer #(.width(16)) demultiplexer_1 (
    .out0(demultiplexer_1_out0), .out1(demultiplexer_1_out1), .in(multiplexer_2_out),
    .sel(_0__destino_0___1__destino_1));  // open: en
  Hex_Digit_Display hex_digit_display_1 (.value(demultiplexer_1_out0[11:8]));  // open: dp
  Hex_Digit_Display hex_digit_display_2 (.value(demultiplexer_1_out0[15:12]));  // open: dp
  Hex_Digit_Display hex_digit_display_3 (.value(demultiplexer_1_out1[15:12]));  // open: dp
  Hex_Digit_Display hex_digit_display_4 (.value(demultiplexer_1_out0[7:4]));  // open: dp
  Hex_Digit_Display hex_digit_display_5 (.value(demultiplexer_1_out1[7:4]));  // open: dp
  Hex_Digit_Display hex_digit_display_6 (.value(demultiplexer_1_out1[11:8]));  // open: dp
  Hex_Digit_Display hex_digit_display_7 (.value(demultiplexer_1_out0[3:0]));  // open: dp
  Hex_Digit_Display hex_digit_display_8 (.value(demultiplexer_1_out1[3:0]));  // open: dp

  // Notes on the sheet:
  //   (3.)
  //   (7.)
  //   (6.)
  //   (2.) RAM
  //   (4.) DMUX
  //   (6.) Clock
  //   (8.) MUX
  //   (2.)
  //   (7.)
  //   (1.) pino de entrada (input)
  //   (3.) Contador de 8 bits
  //   (7.) Pinos de controle diversos
  //   (10.) extensor 8->16 bits
  //   (8.)
  //   (10)
  //   (5.) Display de dígitos (que podem ser substituídos por pinos de saída)
  //   (9.) pino de controle de input: contador=0/input=1
  //   (7.)
  //   (8.)
  //   (4.)
  //   (7.)
  //   destino 0
  //   destino 1
  //   (5.)
  //   (5.)
  //   Projeto de Álgebra Booleana
  //   Arthur Massola
  //   Bruna Thalenberg
endmodule
